// Logisim project ASP02.circ as structural Verilog: 1 circuit, main circuit main
module main (
  input  reset,
  input  [1:0] Input1,
  input  [1:0] Input2,
  input  [1:0] Input3,
  input  [1:0] Input4,
  output [1:0] result
);

  wire clock_out;
  wire [1:0] adder_1_out, multiplier_1_out, register_1_q, register_2_q, register_3_q, register_4_q,
       register_5_q, register_6_q, subtractor_1_out;

  Clock clock (.out(clock_out));
  Register #(.width(2)) register_1 (.D(Input1), .Q(register_1_q), .clk(clock_out), .clr(reset));  // open: en
  Register #(.width(2)) register_2 (.D(Input2), .Q(register_2_q), .clk(clock_out), .clr(reset));  // open: en
  Register #(.width(2)) register_3 (.D(Input3), .Q(register_3_q), .clk(clock_out), .clr(reset));  // open: en
  Register #(.width(2)) register_4 (.D(Input4), .Q(register_4_q), .clk(clock_out), .clr(reset));  // open: en
  Multiplier #(.width(2)) multiplier_1 (.a(register_1_q), .b(register_2_q), .out(multiplier_1_out));  // open: cin, cout
  Adder #(.width(2)) adder_1 (.a(multiplier_1_out), .b(register_3_q), .out(adder_1_out));  // open: cin, cout
  Register #(.width(2)) register_5 (.D(adder_1_out), .Q(register_5_q));  // open: en, clk, clr
  Subtractor #(.width(2)) subtractor_1 (.a(register_5_q), .b(register_6_q), .out(subtractor_1_out));  // open: bin, bout
  Register #(.width(2)) register_6 (.D(register_4_q), .Q(register_6_q));  // open: en, clk, clr
  Register #(.width(2)) register_7 (.D(subtractor_1_out), .Q(result), .clk(clock_out), .clr(reset));  // open: en
endmodule
